# Fritzing sketch Schematic_Button_Led (saved by Fritzing 0.8.7b)
breadboards: 1

parts:
  Raspberry_Pi_B_rev1 = Raspberry Pi B rev2
  S1 = Pushbutton [package="[THT]"]
  LED1 = LED - 5mm [color="Yellow (585nm)" package="5 mm [THT]"]

nets:
  N1: Raspberry_Pi_B_rev1.GPIO_24, LED1.anode
  N2: Raspberry_Pi_B_rev1.GPIO_25, S1.Pin_1, S1.Pin_2
  N3: Raspberry_Pi_B_rev1.GND, S1.Pin_3, S1.Pin_4, LED1.cathode
